# Fritzing sketch BotAstra (saved by Fritzing 0.9.3b)
breadboards: 4

parts:
  hc-sr1 = hc-sr04
  hc-sr3 = hc-sr04
  hc-sr4 = hc-sr04
  Part2 = Arduino Mega ADK (Rev3)
  LED1 = smd LED [color="Yellow (585nm)" package="0603 [SMD]"]  # not connected
  LED2 = smd LED [color="Green (555nm)" package="0603 [SMD]"]  # not connected
  LED3 = smd LED [color="Red (633nm)" package="0603 [SMD]"]  # not connected
  R2 = Resistor [tolerance=±5% resistance=220 package=THT]
  R3 = Resistor [tolerance=±5% resistance=220 package=THT]
  R4 = Resistor [tolerance=±5% resistance=220 package=THT]
  hc-sr2 = hc-sr04
  LED4 = LED - 5mm [color="Green (555nm)" package="5 mm [THT]"]  # not connected
  LED5 = LED - 5mm [color="Red (633nm)" package="5 mm [THT]"]  # not connected
  LED6 = LED - 5mm [color="Yellow (585nm)" package="5 mm [THT]"]  # not connected
  R5 = Resistor [tolerance=±5% resistance=220 package=THT]
  R6 = Resistor [tolerance=±5% resistance=220 package=THT]
  R7 = Resistor [tolerance=±5% resistance=220 package=THT]
  R8 = Resistor [tolerance=±5% resistance=220 package=THT]
  R9 = Resistor [tolerance=±5% resistance=220 package=THT]
  R10 = Resistor [tolerance=±5% resistance=220 package=THT]
  LED7 = LED - 5mm [color="Green (555nm)" package="5 mm [THT]"]  # not connected
  LED8 = LED - 5mm [color="Red (633nm)" package="5 mm [THT]"]  # not connected
  LED9 = LED - 5mm [color="Yellow (585nm)" package="5 mm [THT]"]  # not connected
  LED10 = LED - 5mm [color="Red (633nm)" package="5 mm [THT]"]  # not connected
  LED11 = LED - 5mm [color="Yellow (585nm)" package="5 mm [THT]"]  # not connected
  LED12 = LED - 5mm [color="Green (555nm)" package="5 mm [THT]"]  # not connected
  R11 = Resistor [tolerance=±5% resistance=220 package=THT]
  R12 = Resistor [tolerance=±5% resistance=220 package=THT]
  R13 = Resistor [tolerance=±5% resistance=220 package=THT]

nets:
  VCC: hc-sr1.VCC, hc-sr3.VCC, hc-sr4.VCC, Part2.IOREF, Part2.5V
  N1: hc-sr1.Trig, Part2.D5_PWM
  N2: hc-sr1.Echo, Part2.D4_PWM
  GND: hc-sr1.GND, hc-sr3.GND, hc-sr4.GND, Part2.GND, hc-sr2.GND
  N3: hc-sr3.Trig, Part2.D42
  N4: hc-sr3.Echo, Part2.D40
  N5: hc-sr4.Trig, Part2.D7_PWM
  N6: hc-sr4.Echo, Part2.D6_PWM
  N7: Part2.D29, hc-sr2.Echo
  N8: R2.Pin_0, R3.Pin_1, R4.Pin_0
  N9: R5.Pin_1, R6.Pin_0, R7.Pin_0
  N10: R8.Pin_0, R9.Pin_0, R10.Pin_1
  N11: R11.Pin_0, R12.Pin_1, R13.Pin_0

notes:
  Signal 1
  Signal 4
  Signal 3
  Signal 2
  Archisman Roy
  21JE0152
  BotAstra Project
  Group - 1B

// code stored in the sketch: BotAstra1.fzz.ino

